// Logisim project badApple.circ as structural Verilog: 1 circuit, main circuit main
module main (
  input  Toggle,
  input  Reset
);

  Clock clock_1 ();  // open: out
  ROM #(.addrWidth(12), .dataWidth(64)) rom_1 ();  // open: addr, data
endmodule
